// Logisim project cpu.circ as structural Verilog: 1 circuit, main circuit cpu
module cpu (
);

  wire DataMem_p4, RegisterFile_p7, undriven, undriven_3;
  wire [2:0] undriven_4;
  wire [3:0] undriven_2;
  wire [4:0] multiplexer_2_out;
  wire [31:0] adder_1_out, adder_2_out, alu_1_result, bit_extender_1_out, DataMem_p3, InstMem_p2,
       multiplexer_1_out, multiplexer_3_out, PC_q, RegisterFile_p4, RegisterFile_p5, RegisterFile_p6,
       shifter_1_out;

  Register #(.width(32)) PC (.Q(PC_q));  // open: D, en, clk, clr
  Adder #(.width(32)) adder_1 (.a(PC_q), .b(32'h4), .out(adder_1_out));  // open: cin, cout
  Multiplexer #(.select(2), .width(32)) multiplexer_1 (
    .in0(adder_1_out), .in1(adder_2_out), .in2(alu_1_result), .out(multiplexer_1_out));  // open: in3, sel
  // mem InstMem: pin names not known; wires that end beside it: PC_q, InstMem_p2, InstMem_p2[31:26]
  Multiplexer #(.width(5)) multiplexer_2 (
    .in0(InstMem_p2[20:16]), .in1(InstMem_p2[15:11]), .out(multiplexer_2_out), .sel(undriven));
  assign bit_extender_1_out = {{16{1'b0}}, InstMem_p2[15:0]};  // Bit_Extender bit_extender_1
  // regfile RegisterFile: pin names not known; wires that end beside it: InstMem_p2[25:21], InstMem_p2[20:16], multiplexer_2_out, RegisterFile_p4, RegisterFile_p5, RegisterFile_p6, RegisterFile_p7
  Shifter #(.width(32)) shifter_1 (.in(bit_extender_1_out), .\dist (5'b00010), .out(shifter_1_out));
  Multiplexer #(.width(32)) multiplexer_3 (
    .in0(RegisterFile_p6), .in1(bit_extender_1_out), .out(multiplexer_3_out), .sel(RegisterFile_p7));
  Adder #(.width(32)) adder_2 (.a(adder_1_out), .b(shifter_1_out), .out(adder_2_out));  // open: cin, cout
  ALU alu_1 (
    .reg1(RegisterFile_p5), .reg2(multiplexer_3_out), .shiftAmount(InstMem_p2[10:6]), .operation(undriven_2),
    .isShiftAmount(undriven_3), .branchType(undriven_4), .result(alu_1_result));  // open: zero
  // mem DataMem: pin names not known; wires that end beside it: alu_1_result, RegisterFile_p6, DataMem_p3, DataMem_p4
  Multiplexer #(.width(32)) multiplexer_4 (
    .in0(DataMem_p3), .in1(alu_1_result), .out(RegisterFile_p4), .sel(DataMem_p4));

  // Notes on the sheet:
  //   toControl
  //   from ALUControl
endmodule
